# Fritzing sketch 조도로 서보모터 제어하기 (saved by Fritzing 0.8.7b)
breadboards: 1

parts:
  부품1 = Arduino Uno (Rev3)
  J1 = Basic Servo
  R1 = Resistor [tolerance=±5% resistance=220 package=THT]
  R2 = Photocell (LDR) [package=THT]

nets:
  N1: 부품1.A0, R1.Pin_1, R2.pin_0
  N2: 부품1.D3_PWM, J1.pulse
  5V: 부품1.5V, J1.vcc, R1.Pin_0
  GND: 부품1.GND, J1.gnd, R2.pin_1
